# Fritzing sketch WindowControllerSubsystem (saved by Fritzing 1.0.4)
breadboards: 1

parts:
  Componente1 = Arduino Uno (Rev3)
  LCD2004-I2C1 = LCD2004-I2C
  S1 = Pushbutton [package="[THT]"]
  R1 = Resistor [tolerance=±5% resistance=10k package="2010 [SMD]"]
  R2 = Trimmer Potentiometer [maximum_resistance=10kΩ knob_status=50% power=0.5W package=THT]
  J1 = Basic Servo
  T1 = LM35 Temperature Sensor [package="TO92 [THT]"]
  M1 = ESP32-C3-DevKitC-02 [part_number=ESP32-C3-DevKitC-02]
  LED2 = LED - 5mm [color="Red (633nm)" current=0.030A package="5 mm [THT]"]
  LED3 = LED - 5mm [color="Green (555nm)" current=0.030A package="5 mm [THT]"]
  R3 = Resistor [tolerance=±5% resistance=220 package="0402 [SMD]"]
  R4 = Resistor [tolerance=±5% resistance=220 package="0402 [SMD]"]

nets:
  N1: Componente1.A0, R2.wiper
  N2: Componente1.A3, J1.pulse
  N3: Componente1.D13/SCK, S1.Pin_3, S1.Pin_4, R1.Pin_1
  N4: Componente1.A4/SDA, LCD2004-I2C1.SDA
  N5: Componente1.A5/SCL, LCD2004-I2C1.SCL
  VCC: Componente1.5V, LCD2004-I2C1.VCC, S1.Pin_1, S1.Pin_2, R2.leg2, J1.vcc, T1.+Vs
  GND: Componente1.GND, LCD2004-I2C1.GND, R1.Pin_0, R2.leg1, J1.gnd, T1.GND
  N6: T1.Vout, M1.5
  N7: M1.3, LED2.anode
  N8: M1.2, LED3.anode
  N9: M1.GND, R3.Pin_1, R4.Pin_1
  N10: LED2.cathode, R4.Pin_0
  N11: LED3.cathode, R3.Pin_0

notes:
  Window Controller Subsystem
  - Luca Casadei 0001069237
  - Francesco Pazzaglia 0001077423

custom parts:
  LCD2004-I2C: A standard character display with 4x20 characters. Comes in many colors with LCM2004 IIC attached.
  ESP32-C3-DevKitC-02: Esp32-C3 DevKitC 02 is one of the development board created by Espressif. It is based on the ESP32 microcontroller that boasts Wifi, Bluetooth, Ethernet and Low Power support all in a single chip. (vanepp) Feb 2021: converted to ESP32-C3-DevKitC-02. This chip is 30pins long (2 x15) and 11 pins width.
