# Fritzing sketch Schema (saved by Fritzing 1.0.4)
breadboards: 1

parts:
  Componente1 = Arduino Uno (Rev3)
  HC-SR04_Sensor_1 = HC-SR04 Ultrasonic Distance Sensor  # not connected
  T1 = TMP36 Temperature Sensor [package="TO92 [THT]"]  # not connected
  LCD2004-I2C1 = LCD2004-I2C
  J1 = Basic Servo  # not connected
  S1 = Pushbutton [package="[THT]"]
  S2 = Pushbutton [package="[THT]"]
  R1 = Resistor [tolerance=±5% power=0.25W resistance=220 package=THT]
  R2 = Resistor [tolerance=±5% power=0.25W resistance=220 package=THT]
  R3 = Resistor [tolerance=±5% power=0.25W resistance=10k package=THT]
  R4 = Resistor [tolerance=±5% power=0.25W resistance=10k package=THT]
  PIR1 = PIR sensor
  LED3 = smd LED [color="Red (633nm)" package="0603 [SMD]"]
  LED4 = smd LED [color="Green (555nm)" package="0603 [SMD]"]

nets:
  N1: Componente1.A5/SCL, LCD2004-I2C1.SCL, PIR1.SIG
  N2: Componente1.D12/MISO, S1.Pin_3, S1.Pin_4, R4.Pin_0
  N3: Componente1.D13/SCK, S2.Pin_3, S2.Pin_4, R3.Pin_0
  N4: Componente1.A4/SDA, LCD2004-I2C1.SDA
  N5: Componente1.D2, LED3.anode
  N6: Componente1.D3_PWM, LED4.anode
  5V: Componente1.5V, LCD2004-I2C1.VCC, S1.Pin_1, S1.Pin_2, S2.Pin_1, S2.Pin_2, PIR1.VDD
  GND: Componente1.GND, LCD2004-I2C1.GND, R1.Pin_0, R2.Pin_0, R3.Pin_1, R4.Pin_1, PIR1.GND
  N7: R1.Pin_1, LED3.cathode
  N8: R2.Pin_1, LED4.cathode

custom parts:
  LCD2004-I2C: A standard character display with 4x20 characters. Comes in many colors with LCM2004 IIC attached.
